# Fritzing sketch amperimetro-dos-resistencias-en-serie (saved by Fritzing 1.0.0rc)
breadboards: 1

parts:
  VCC1 = 4 x AAA Battery Mount
  R3 = Resistor [tolerance=±5% power=0.25W resistance=220 package=THT]
  OM1 = Multimeter (DC Current)
  R4 = Resistor [tolerance=±5% power=0.25W resistance=220 package=THT]

nets:
  N1: VCC1.-, OM1.COM_Probe
  N2: VCC1.+, R3.Pin_1
  N3: R3.Pin_0, R4.Pin_1
  N4: OM1.A_Probe, R4.Pin_0
