# Fritzing sketch corto-circuito-1 (saved by Fritzing 1.0.0rc)
breadboards: 1

parts:
  LED1 = LED - 5mm [color="Red (633nm)" current=0.030A package="5 mm [THT]"]
  AM1 = Multimeter (DC Current)
  AM2 = Multimeter (DC Current)
  S6 = Pushbutton [package=THT]
  VCC1 = Battery
  AM3 = Multimeter (DC Current)
  R1 = Resistor [tolerance=±5% power=0.25W resistance=220 package=THT]

nets:
  N1: LED1.cathode, AM1.A_Probe
  N2: LED1.anode, AM2.A_Probe, S6.leg1, R1.Pin_0
  GND: AM1.COM_Probe, AM2.COM_Probe, VCC1.-, AM3.COM_Probe
  N3: S6.leg0, VCC1.+
  N4: AM3.A_Probe, R1.Pin_1
