# Fritzing sketch corto-circuito-2 (saved by Fritzing 1.0.0rc)
breadboards: 1

parts:
  AM2 = Multimeter (DC Current)
  VCC1 = Battery
  VCC2 = Battery
  S7 = Pushbutton [package=THT]
  R1 = Resistor [tolerance=±5% power=0.25W resistance=10 package=THT]
  AM4 = Multimeter (DC Voltage)
  AM5 = Multimeter (DC Voltage)
  S6 = Pushbutton [package=THT]
  AM3 = Multimeter (DC Current)
  AM6 = Multimeter (DC Voltage)
  AM7 = Multimeter (DC Voltage)

nets:
  GND: AM2.COM_Probe, VCC1.-, VCC2.-, AM4.COM_Probe, AM4.V_Probe, AM5.COM_Probe, AM5.V_Probe, AM3.COM_Probe, AM6.COM_Probe, AM7.COM_Probe
  N1: AM2.A_Probe, S6.leg1
  N2: VCC1.+, S6.leg0, AM7.V_Probe
  N3: VCC2.+, S7.leg0, AM6.V_Probe
  N4: S7.leg1, R1.Pin_0
  N5: R1.Pin_1, AM3.A_Probe
