# Fritzing sketch corto-circuito-3 (saved by Fritzing 1.0.0rc)
breadboards: 1

parts:
  R1 = Resistor [tolerance=±5% power=0.25W resistance=220 package=THT]
  LED1 = LED - 5mm [color="Red (633nm)" current=0.030A package="5 mm [THT]"]
  VCC1 = 4 x AAA Battery Mount
  AM1 = Multimeter (DC Current)
  AM2 = Multimeter (DC Current)
  AM3 = Multimeter (DC Current)
  S1 = Pushbutton [package=THT]
  AM4 = Multimeter (DC Voltage)
  AM5 = Multimeter (DC Voltage)
  R2 = Resistor [tolerance=±5% power=0.25W resistance=0 package=THT]
  AM6 = Multimeter (DC Voltage)

nets:
  N1: R1.Pin_0, AM1.COM_Probe, AM6.V_Probe
  N2: R1.Pin_1, AM2.A_Probe, AM3.A_Probe, AM6.COM_Probe
  GND: LED1.cathode, VCC1.-, AM4.COM_Probe, AM5.COM_Probe, R2.Pin_1
  N3: LED1.anode, AM2.COM_Probe, AM4.V_Probe
  N4: VCC1.+, S1.leg0
  N5: AM1.A_Probe, S1.leg1
  N6: AM3.COM_Probe, AM5.V_Probe, R2.Pin_0
