# Fritzing sketch corto-circuito-con-amperimetro (saved by Fritzing 1.0.0rc)
breadboards: 1

parts:
  R2 = Resistor [tolerance=±5% power=0.25W resistance=220 package=THT]
  VCC2 = 4 x AAA Battery Mount
  LED2 = LED - 5mm [color="Red (633nm)" current=0.030A package="5 mm [THT]"]
  AM1 = Multimeter (DC Current)
  AM2 = Multimeter (DC Current)
  R3 = Resistor [tolerance=±5% power=0.25W resistance=0 package=THT]
  AM3 = Multimeter (DC Current)
  S2 = Pushbutton [package=THT]

nets:
  N1: R2.Pin_0, AM1.COM_Probe
  N2: R2.Pin_1, AM2.A_Probe, AM3.A_Probe
  N3: VCC2.-, LED2.cathode, R3.Pin_1
  N4: VCC2.+, S2.leg0
  N5: LED2.anode, AM2.COM_Probe
  N6: AM1.A_Probe, S2.leg1
  N7: R3.Pin_0, AM3.COM_Probe
