# Fritzing sketch corto-circuito-sin-amperimetro (saved by Fritzing 1.0.0rc)
breadboards: 1

parts:
  R2 = Resistor [tolerance=±5% power=0.25W resistance=220 package=THT]
  VCC2 = 4 x AAA Battery Mount
  LED2 = LED - 5mm [color="Red (633nm)" current=0.030A package="5 mm [THT]"]
  R3 = Resistor [tolerance=±5% power=0.25W resistance=0 package=THT]
  S2 = Pushbutton [package=THT]

nets:
  N1: R2.Pin_0, S2.leg1
  N2: R2.Pin_1, LED2.anode, R3.Pin_0
  N3: VCC2.-, LED2.cathode, R3.Pin_1
  N4: VCC2.+, S2.leg0
