# Fritzing sketch divisor-de-tension-con-dos-resistencias (saved by Fritzing 1.0.0rc)
breadboards: 1

parts:
  R1 = Resistor [tolerance=±5% power=0.25W resistance=220 package=THT]
  VCC1 = Battery
  VM1 = Multimeter (DC Voltage)
  R2 = Resistor [tolerance=±5% power=0.25W resistance=220 package=THT]
  VM2 = Multimeter (DC Voltage)
  VM3 = Multimeter (DC Current)
  R3 = Resistor [tolerance=±5% power=0.25W resistance=1k package=THT]
  R4 = Resistor [tolerance=±5% power=0.25W resistance=1k package=THT]
  VCC2 = Battery
  VM4 = Multimeter (DC Current)
  VM5 = Multimeter (DC Voltage)
  VM6 = Multimeter (DC Voltage)

nets:
  N1: R1.Pin_0, VCC1.+, VM1.V_Probe
  N2: R1.Pin_1, VM1.COM_Probe, R2.Pin_0, VM2.V_Probe
  GND: VCC1.-, VM3.COM_Probe, VCC2.-, VM4.COM_Probe
  N3: R2.Pin_1, VM2.COM_Probe, VM3.A_Probe
  N4: R3.Pin_0, VCC2.+, VM5.V_Probe
  N5: R3.Pin_1, R4.Pin_0, VM5.COM_Probe, VM6.V_Probe
  N6: R4.Pin_1, VM4.A_Probe, VM6.COM_Probe
