# Fritzing sketch divisor-de-tension-con-potenciometro-escenarios (saved by Fritzing 1.0.0rc)
breadboards: 1

parts:
  R1 = Resistor [tolerance=±5% power=0.25W resistance=7k package=THT]
  VM1 = Multimeter (DC Voltage)
  P1 = Rotary Potentiometer (Small) [maximum_resistance=3k knob_status=60% power=0.5W package=THT]
  VCC1 = Battery block 9V
  VM2 = Multimeter (DC Voltage)
  VM3 = Multimeter (DC Voltage)
  S1 = Pushbutton [package=THT]
  R6 = Resistor [tolerance=±5% power=0.25W resistance=7k package=THT]
  R7 = Resistor [tolerance=±5% power=0.25W resistance=1.8k package=THT]
  R8 = Resistor [tolerance=±5% power=0.25W resistance=1.2k package=THT]
  VCC2 = Battery block 9V
  VM8 = Multimeter (DC Current)
  VM9 = Multimeter (DC Voltage)
  VM10 = Multimeter (DC Voltage)
  VM11 = Multimeter (DC Voltage)
  S2 = Pushbutton [package=THT]
  R9 = Resistor [tolerance=±5% power=0.25W resistance=7k package=THT]
  VCC3 = Battery block 9V
  VM12 = Multimeter (DC Voltage)
  VM13 = Multimeter (DC Voltage)
  VM14 = Multimeter (DC Voltage)
  P2 = Rotary Potentiometer (Small) [maximum_resistance=3k knob_status=0.1k% power=0.5W package=THT]
  S3 = Pushbutton [package=THT]
  VCC4 = Battery block 9V
  VM15 = Multimeter (DC Voltage)
  VM17 = Multimeter (DC Voltage)
  P3 = Rotary Potentiometer (Small) [maximum_resistance=10kΩ knob_status=50% power=0.5W package=THT]
  VM18 = Multimeter (DC Voltage)
  P4 = Rotary Potentiometer (Small) [maximum_resistance=10kΩ knob_status=25% power=0.25W package=THT]
  VCC5 = Battery block 9V
  VM19 = Multimeter (DC Voltage)
  VM20 = Multimeter (DC Voltage)
  VM21 = Multimeter (DC Voltage)
  VM22 = Multimeter (DC Current)
  VM23 = Multimeter (DC Current)
  VM24 = Multimeter (DC Current)
  VM25 = Multimeter (DC Current)
  P5 = Rotary Potentiometer (Small) [maximum_resistance=10kΩ knob_status=75% power=0.5W package=THT]
  VCC6 = Battery block 9V
  VM26 = Multimeter (DC Voltage)
  VM27 = Multimeter (DC Current)
  VM28 = Multimeter (DC Current)
  VM29 = Multimeter (DC Voltage)
  VM30 = Multimeter (DC Voltage)
  R10 = Resistor [tolerance=±5% power=0.25W resistance=1.5k package=THT]
  VM31 = Multimeter (DC Voltage)
  P6 = Rotary Potentiometer (Small) [maximum_resistance=10kΩ knob_status=0.1k% power=0.5W package=THT]
  VCC7 = Battery block 9V
  VM32 = Multimeter (DC Current)
  VM33 = Multimeter (DC Voltage)
  VM34 = Multimeter (DC Current)
  VM35 = Multimeter (DC Voltage)
  VM36 = Multimeter (DC Voltage)
  VM37 = Multimeter (DC Voltage)
  R11 = Resistor [tolerance=±5% power=0.25W resistance=1.5k package=THT]
  VCC8 = Battery block 9V
  VM39 = Multimeter (DC Current)
  VM40 = Multimeter (DC Current)
  VM41 = Multimeter (DC Voltage)
  VM42 = Multimeter (DC Voltage)
  R12 = Resistor [tolerance=±5% power=0.25W resistance=1.5k package=THT]
  P7 = Rotary Potentiometer (Small) [maximum_resistance=10kΩ knob_status=25% power=0.5W package=THT]  # not connected
  R13 = Resistor [tolerance=±5% power=0.25W resistance=10k package=THT]
  VCC9 = Battery block 9V
  VM43 = Multimeter (DC Current)
  VM46 = Multimeter (DC Voltage)
  R14 = Resistor [tolerance=±5% power=0.25W resistance=2.5k package=THT]
  VCC10 = Battery block 9V
  VM47 = Multimeter (DC Current)
  VM48 = Multimeter (DC Voltage)
  R15 = Resistor [tolerance=±5% power=0.25W resistance=5k package=THT]
  VCC11 = Battery block 9V
  VM49 = Multimeter (DC Current)
  VM50 = Multimeter (DC Voltage)
  R16 = Resistor [tolerance=±5% power=0.25W resistance=10k package=THT]
  VCC12 = Battery block 9V
  VM51 = Multimeter (DC Current)
  VM52 = Multimeter (DC Voltage)
  R17 = Resistor [tolerance=±5% power=0.25W resistance=2.2k package=THT]

nets:
  N1: R1.Pin_0, VM1.V_Probe, S1.leg1
  N2: R1.Pin_1, VM1.COM_Probe, P1.leg1, VM2.V_Probe, VM3.V_Probe
  N3: P1.wiper, VM3.COM_Probe
  GND: P1.leg2, VCC1.-, VM2.COM_Probe, VCC2.-, VM8.COM_Probe, VCC3.-, VM13.COM_Probe, P2.wiper, VCC4.-, VCC5.-, VM24.COM_Probe, VM25.COM_Probe, VCC6.-, VM27.COM_Probe, VCC7.-, VM32.COM_Probe, VCC8.-, VM39.COM_Probe
  N4: VCC1.+, S1.leg0
  N5: R6.Pin_0, VM9.V_Probe, S2.leg1
  N6: R6.Pin_1, R7.Pin_0, VM9.COM_Probe, VM11.V_Probe
  N7: R7.Pin_1, R8.Pin_0, VM10.V_Probe, VM11.COM_Probe
  N8: R8.Pin_1, VM8.A_Probe, VM10.COM_Probe
  N9: VCC2.+, S2.leg0
  N10: R9.Pin_0, VM12.V_Probe, S3.leg1
  N11: R9.Pin_1, VM12.COM_Probe, VM13.V_Probe, VM14.V_Probe, P2.leg1
  N12: VCC3.+, S3.leg0
  N13: VM14.COM_Probe, P2.leg2
  N14: VCC4.+, VM23.A_Probe
  N15: VM15.COM_Probe, P3.wiper, VM18.V_Probe
  N16: VM15.V_Probe, VM17.V_Probe, P3.leg1, VM23.COM_Probe
  N17: VM17.COM_Probe, P3.leg2, VM18.COM_Probe, VM25.A_Probe
  N18: P4.leg1, VM20.V_Probe, VM21.V_Probe, VM22.COM_Probe
  N19: P4.wiper, VM19.V_Probe, VM21.COM_Probe, VM24.A_Probe
  N20: P4.leg2, VM19.COM_Probe, VM20.COM_Probe
  N21: VCC5.+, VM22.A_Probe
  N22: P5.leg1, VM28.COM_Probe, VM29.V_Probe, VM30.V_Probe
  N23: P5.wiper, VM26.V_Probe, VM30.COM_Probe
  N24: P5.leg2, VM26.COM_Probe, VM27.A_Probe, VM29.COM_Probe
  N25: VCC6.+, R10.Pin_1, VM31.V_Probe
  N26: VM28.A_Probe, R10.Pin_0, VM31.COM_Probe
  N27: P6.leg1, VM34.COM_Probe, VM35.V_Probe, VM36.V_Probe
  N28: P6.wiper, VM32.A_Probe, VM33.V_Probe, VM36.COM_Probe
  N29: P6.leg2, VM33.COM_Probe, VM35.COM_Probe
  N30: VCC7.+, VM37.V_Probe, R11.Pin_1
  N31: VM34.A_Probe, VM37.COM_Probe, R11.Pin_0
  N32: VCC8.+, VM42.V_Probe, R12.Pin_1
  N33: VM39.A_Probe, VM41.COM_Probe, R13.Pin_0
  N34: VM40.COM_Probe, VM41.V_Probe, R13.Pin_1
  N35: VM40.A_Probe, VM42.COM_Probe, R12.Pin_0
  N36: VCC9.-, VM43.COM_Probe
  N37: VCC9.+, VM46.V_Probe, R14.Pin_1
  N38: VM43.A_Probe, VM46.COM_Probe, R14.Pin_0
  N39: VCC10.-, VM47.COM_Probe
  N40: VCC10.+, VM48.V_Probe, R15.Pin_1
  N41: VM47.A_Probe, VM48.COM_Probe, R15.Pin_0
  N42: VCC11.-, VM49.COM_Probe
  N43: VCC11.+, VM50.V_Probe, R16.Pin_1
  N44: VM49.A_Probe, VM50.COM_Probe, R16.Pin_0
  N45: VCC12.-, VM51.COM_Probe
  N46: VCC12.+, VM52.V_Probe, R17.Pin_1
  N47: VM51.A_Probe, VM52.COM_Probe, R17.Pin_0
