# Fritzing sketch divisor-de-tension-con-tres-resistencias (saved by Fritzing 1.0.0rc)
breadboards: 1

parts:
  R1 = Resistor [tolerance=±5% power=0.25W resistance=220 package=THT]
  VM1 = Multimeter (DC Voltage)
  R2 = Resistor [tolerance=±5% power=0.25W resistance=220 package=THT]
  VM2 = Multimeter (DC Voltage)
  VM3 = Multimeter (DC Current)
  R5 = Resistor [tolerance=±5% power=0.25W resistance=470 package=THT]
  VM7 = Multimeter (DC Voltage)
  VCC1 = Battery block 9V

nets:
  N1: R1.Pin_0, VM1.V_Probe, R5.Pin_1, VM7.COM_Probe
  N2: R1.Pin_1, VM1.COM_Probe, R2.Pin_0, VM2.V_Probe
  N3: R2.Pin_1, VM2.COM_Probe, VM3.A_Probe
  GND: VM3.COM_Probe, VCC1.-
  N4: R5.Pin_0, VM7.V_Probe, VCC1.+
