# Fritzing sketch dos-resistencias-en-serie-2 (saved by Fritzing 1.0.0rc)
breadboards: 1

parts:
  R1 = Resistor [tolerance=±5% power=0.25W resistance=150 package=THT]
  R2 = Resistor [tolerance=±5% power=0.25W resistance=220 package=THT]
  AM1 = Multimeter (DC Current)
  AM2 = Multimeter (DC Voltage)  # not connected
  VCC1 = 4 x AAA Battery Mount

nets:
  N1: R1.Pin_0, AM1.COM_Probe, VCC1.-
  N2: R1.Pin_1, R2.Pin_0, AM1.A_Probe
  GND: R2.Pin_1, VCC1.+
