# Fritzing sketch dos-resistencias-en-serie-3 (saved by Fritzing 1.0.0rc)
breadboards: 1

parts:
  R1 = Resistor [tolerance=±5% power=0.25W resistance=220 package=THT]
  R2 = Resistor [tolerance=±5% power=0.25W resistance=220 package=THT]
  VCC1 = Battery

nets:
  N1: R1.Pin_0, VCC1.-
  N2: R1.Pin_1, R2.Pin_0
  GND: R2.Pin_1, VCC1.+
