# Fritzing sketch ohmetro-dos-resistencias-en-paralelo-1 (saved by Fritzing 1.0.0rc)
breadboards: 1

parts:
  OM1 = Multimeter (Ohmmeter)
  R3 = Resistor [tolerance=±5% power=0.25W resistance=220 package=THT]
  R4 = Resistor [tolerance=±5% power=0.25W resistance=220 package=THT]

nets:
  N1: OM1.COM_Probe, R3.Pin_0, R4.Pin_0
  N2: OM1.V_Probe, R3.Pin_1, R4.Pin_1
