# Fritzing sketch ohmetro-resistencias-en-serie-y-paralelo (saved by Fritzing 1.0.0rc)
breadboards: 1

parts:
  OM1 = Multimeter (Ohmmeter)
  R1 = Resistor [tolerance=±5% power=0.25W resistance=220 package=THT]
  R3 = Resistor [tolerance=±5% power=0.25W resistance=220 package=THT]
  R4 = Resistor [tolerance=±5% power=0.25W resistance=220 package=THT]

nets:
  N1: OM1.COM_Probe, R3.Pin_1, R4.Pin_1
  N2: OM1.V_Probe, R1.Pin_0
  N3: R1.Pin_1, R3.Pin_0, R4.Pin_0
