# Fritzing sketch ohmetro-tres-resistencias-en-serie-1 (saved by Fritzing 1.0.0rc)
breadboards: 1

parts:
  R1 = Resistor [tolerance=±5% power=0.25W resistance=220 package=THT]
  R2 = Resistor [tolerance=±5% power=0.25W resistance=220 package=THT]
  OM1 = Multimeter (Ohmmeter)
  R3 = Resistor [tolerance=±5% power=0.25W resistance=220 package=THT]

nets:
  N1: R1.Pin_0, R3.Pin_1
  N2: R1.Pin_1, R2.Pin_0
  N3: R2.Pin_1, OM1.V_Probe
  N4: OM1.COM_Probe, R3.Pin_0
