# Fritzing sketch potenciometro-buzzer-con-pines2y3 (saved by Fritzing 1.0.0rc)
breadboards: 1

parts:
  R2 = Resistor [tolerance=±5% power=0.25W resistance=220 package=THT]
  VCC1 = Battery block 9V
  R1 = Rotary Potentiometer (Small) [maximum_resistance=10kΩ knob_status=100% power=0.5W package=THT]
  SPKR1 = Loudspeaker

nets:
  N1: R2.Pin_0, SPKR1.pin1
  N2: R2.Pin_1, VCC1.-
  N3: VCC1.+, R1.leg2
  N4: R1.wiper, SPKR1.pin2
