# Fritzing sketch potenciometro-led-con-pines1y2-con-voltimetro (saved by Fritzing 1.0.0rc)
breadboards: 1

parts:
  R5 = Rotary Potentiometer (Small) [maximum_resistance=10kΩ knob_status=0% power=0.5W package=THT]
  R6 = Resistor [tolerance=±5% power=0.25W resistance=330 package=THT]
  VCC3 = Battery block 9V
  LED3 = LED - 5mm [color="Red (633nm)" current=0.030A package="5 mm [THT]"]
  AM3 = Multimeter (DC Voltage)
  AM4 = Multimeter (DC Voltage)

nets:
  N1: R5.leg1, VCC3.+, AM3.V_Probe
  N2: R5.wiper, R6.Pin_1, AM3.COM_Probe
  N3: R6.Pin_0, LED3.anode, AM4.V_Probe
  N4: VCC3.-, LED3.cathode, AM4.COM_Probe
