# Fritzing sketch potenciometro-led-con-pines1y2y3 (saved by Fritzing 1.0.0rc)
breadboards: 1

parts:
  R2 = Resistor [tolerance=±5% power=0.25W resistance=330 package=THT]
  LED1 = LED - 5mm [color="Red (633nm)" current=0.030A package="5 mm [THT]"]
  VCC1 = Battery block 9V
  R1 = Rotary Potentiometer (Small) [maximum_resistance=10kΩ knob_status=0% power=0.5W package=THT]

nets:
  N1: R2.Pin_0, LED1.cathode
  N2: R2.Pin_1, VCC1.-, R1.leg2
  N3: LED1.anode, R1.wiper
  N4: VCC1.+, R1.leg1
