# Fritzing sketch potenciometro-led-con-pines2y3-con-amperimetro (saved by Fritzing 1.0.0rc)
breadboards: 1

parts:
  R2 = Resistor [tolerance=±5% power=0.25W resistance=330 package=THT]
  LED1 = LED - 5mm [color="Red (633nm)" current=0.030A package="5 mm [THT]"]
  VCC1 = Battery block 9V
  R1 = Rotary Potentiometer (Small) [maximum_resistance=10kΩ knob_status=0.1k% power=0.5W package=THT]
  AM1 = Multimeter (DC Current)

nets:
  N1: R2.Pin_0, LED1.cathode
  N2: R2.Pin_1, VCC1.-
  N3: LED1.anode, R1.wiper
  N4: VCC1.+, AM1.A_Probe
  N5: R1.leg2, AM1.COM_Probe
