# Fritzing sketch resistencia-para-dos-leds-con-amperimetro (saved by Fritzing 1.0.0rc)
breadboards: 1

parts:
  LED1 = LED - 5mm [color="Red (633nm)" current=30mA package="5 mm [THT]"]
  R3 = Resistor [tolerance=±5% power=0.25W resistance=220 package=THT]
  VCC1 = Battery block 9V
  LED2 = LED - 5mm [color="Red (660nm)" current=30mA package="5 mm [THT]"]
  VM4 = Multimeter (DC Current)
  VM5 = Multimeter (DC Current)
  VM6 = Multimeter (DC Current)

nets:
  N1: LED1.cathode, VM6.A_Probe
  N2: LED1.anode, VM5.COM_Probe
  N3: R3.Pin_0, VM5.A_Probe
  N4: R3.Pin_1, VM4.COM_Probe
  GND: VCC1.-, LED2.cathode
  N5: VCC1.+, VM4.A_Probe
  N6: LED2.anode, VM6.COM_Probe
