# Fritzing sketch resistencia-para-dos-leds-con-voltimetro (saved by Fritzing 1.0.0rc)
breadboards: 1

parts:
  VM3 = Multimeter (DC Voltage)
  LED1 = LED - 5mm [color="Red (633nm)" current=30mA package="5 mm [THT]"]
  R3 = Resistor [tolerance=±5% power=0.25W resistance=220 package=THT]
  VCC1 = Battery block 9V
  VM2 = Multimeter (DC Voltage)
  VM1 = Multimeter (DC Voltage)
  LED2 = LED - 5mm [color="Red (660nm)" current=30mA package="5 mm [THT]"]

nets:
  GND: VM3.COM_Probe, VCC1.-, LED2.cathode
  N1: VM3.V_Probe, LED1.cathode, VM2.COM_Probe, LED2.anode
  N2: LED1.anode, R3.Pin_0, VM2.V_Probe, VM1.COM_Probe
  N3: R3.Pin_1, VCC1.+, VM1.V_Probe
