# Fritzing sketch resistencia-para-dos-leds-en-paralelo-1 (saved by Fritzing 1.0.0rc)
breadboards: 1

parts:
  R3 = Resistor [tolerance=±5% power=0.25W resistance=220 package=THT]
  LED2 = LED - 5mm [color="Red (633nm)" current=0.030A package="5 mm [THT]"]
  AM1 = Multimeter (DC Current)
  AM2 = Multimeter (DC Current)
  LED3 = LED - 5mm [color="Red (633nm)" current=0.030A package="5 mm [THT]"]
  VCC1 = Battery block 9V

nets:
  N1: R3.Pin_0, VCC1.+
  N2: R3.Pin_1, AM1.A_Probe
  GND: LED2.cathode, LED3.cathode, VCC1.-
  N3: LED2.anode, AM1.COM_Probe, AM2.A_Probe
  N4: AM2.COM_Probe, LED3.anode
