# Fritzing sketch resistencia-para-dos-leds-en-paralelo-2 (saved by Fritzing 1.0.0rc)
breadboards: 1

parts:
  R3 = Resistor [tolerance=±5% power=0.25W resistance=68 package=THT]
  VCC1 = 4 x AAA Battery Mount
  AM1 = Multimeter (DC Current)
  LED5 = LED - 5mm [color="Red (633nm)" current=0.030A package="5 mm [THT]"]
  LED6 = LED - 5mm [color="Red (633nm)" current=0.030A package="5 mm [THT]"]

nets:
  N1: R3.Pin_0, VCC1.+
  N2: R3.Pin_1, AM1.A_Probe
  GND: VCC1.-, LED5.cathode, LED6.cathode
  N3: AM1.COM_Probe, LED5.anode, LED6.anode
