# Fritzing sketch resistencia-para-dos-leds-en-paralelo-con-amperimetro-3 (saved by Fritzing 1.0.0rc)
breadboards: 1

parts:
  R3 = Resistor [tolerance=±5% power=0.25W resistance=220 package=THT]
  AM1 = Multimeter (DC Current)
  VCC1 = Battery block 9V
  AM2 = Multimeter (DC Current)
  LED3 = LED - 5mm [color="Red (633nm)" current=0.030A package="5 mm [THT]"]
  LED4 = LED - 5mm [color="Red (633nm)" current=0.030A package="5 mm [THT]"]

nets:
  N1: R3.Pin_0, VCC1.+
  N2: R3.Pin_1, AM1.A_Probe
  N3: AM1.COM_Probe, LED3.anode, LED4.anode
  GND: VCC1.-, AM2.COM_Probe, LED4.cathode
  N4: AM2.A_Probe, LED3.cathode
