# Fritzing sketch resistencia-para-dos-leds-en-paralelo-con-voltimetro-amperimetro (saved by Fritzing 1.0.0rc)
breadboards: 1

parts:
  R3 = Resistor [tolerance=±5% power=0.25W resistance=47 package=THT]
  LED2 = LED - 5mm [color="Red (633nm)" current=0.030A package="5 mm [THT]"]
  LED3 = LED - 5mm [color="Red (633nm)" current=0.030A package="5 mm [THT]"]
  VCC1 = 4 x AAA Battery Mount
  AM3 = Multimeter (DC Current)
  AM4 = Multimeter (DC Current)
  AM5 = Multimeter (DC Current)
  AM6 = Multimeter (DC Current)
  AM7 = Multimeter (DC Current)
  AM8 = Multimeter (DC Current)
  AM9 = Multimeter (DC Voltage)
  AM10 = Multimeter (DC Voltage)
  AM11 = Multimeter (DC Voltage)

nets:
  N1: R3.Pin_0, AM3.COM_Probe, AM11.V_Probe
  N2: R3.Pin_1, AM4.A_Probe, AM5.A_Probe, AM11.COM_Probe
  N3: LED2.cathode, AM7.A_Probe, AM9.COM_Probe
  N4: LED2.anode, AM4.COM_Probe, AM9.V_Probe
  N5: LED3.cathode, AM6.A_Probe, AM10.COM_Probe
  N6: LED3.anode, AM5.COM_Probe, AM10.V_Probe
  GND: VCC1.-, AM8.A_Probe
  N7: VCC1.+, AM3.A_Probe
  N8: AM6.COM_Probe, AM7.COM_Probe, AM8.COM_Probe
