# Fritzing sketch resistencia-para-dos-leds-en-paralelo-con-voltimetro (saved by Fritzing 1.0.0rc)

parts:
  LED5 = LED - 5mm [color="Red (633nm)" current=0.030A package="5 mm [THT]"]
  LED6 = LED - 5mm [color="Red (633nm)" current=0.030A package="5 mm [THT]"]
  AM4 = Multimeter (DC Voltage)
  AM5 = Multimeter (DC Voltage)
  AM6 = Multimeter (DC Voltage)
  VCC2 = 4 x AAA Battery Mount
  R4 = Resistor [tolerance=±5% power=0.25W resistance=47 package=THT]

nets:
  GND: LED5.cathode, LED6.cathode, AM5.COM_Probe, AM6.COM_Probe, VCC2.-
  N1: LED5.anode, LED6.anode, AM4.COM_Probe, AM5.V_Probe, AM6.V_Probe, R4.Pin_1
  N2: AM4.V_Probe, VCC2.+, R4.Pin_0
