# Fritzing sketch resistencia-para-tres-leds-en-paralelo-1 (saved by Fritzing 1.0.0rc)
breadboards: 1

parts:
  R1 = Resistor [tolerance=±5% power=0.25W resistance=220 package=THT]
  LED1 = LED - 5mm [color="Red (633nm)" current=30mA package="5 mm [THT]"]
  LED2 = LED - 5mm [color="Red (633nm)" current=30mA package="5 mm [THT]"]
  LED3 = LED - 5mm [color="Red (633nm)" current=30mA package="5 mm [THT]"]
  VCC1 = Battery block 9V
  AM1 = Multimeter (DC Current)
  AM2 = Multimeter (DC Current)
  AM3 = Multimeter (DC Current)
  AM4 = Multimeter (DC Current)
  AM5 = Multimeter (DC Voltage)
  AM6 = Multimeter (DC Voltage)
  AM7 = Multimeter (DC Voltage)
  AM8 = Multimeter (DC Voltage)

nets:
  N1: R1.Pin_0, AM1.COM_Probe, AM8.V_Probe
  N2: R1.Pin_1, AM2.A_Probe, AM3.A_Probe, AM4.A_Probe, AM8.COM_Probe
  GND: LED1.cathode, LED2.cathode, LED3.cathode, VCC1.-, AM5.COM_Probe, AM6.COM_Probe, AM7.COM_Probe
  N3: LED1.anode, AM2.COM_Probe, AM5.V_Probe
  N4: LED2.anode, AM3.COM_Probe, AM6.V_Probe
  N5: LED3.anode, AM4.COM_Probe, AM7.V_Probe
  N6: VCC1.+, AM1.A_Probe
