# Fritzing sketch resistencia-para-un-led-1-con-voltimetro (saved by Fritzing 1.0.0rc)
breadboards: 1

parts:
  R3 = Resistor [tolerance=±5% power=0.25W resistance=220 package=THT]
  LED1 = LED - 5mm [color="Red (633nm)" current=20mA package="5 mm [THT]"]
  VCC1 = 4 x AAA Battery Mount
  VM1 = Multimeter (DC Voltage)
  VM2 = Multimeter (DC Voltage)

nets:
  N1: R3.Pin_0, LED1.anode, VM1.COM_Probe, VM2.V_Probe
  N2: R3.Pin_1, VCC1.+, VM1.V_Probe
  N3: LED1.cathode, VCC1.-, VM2.COM_Probe
