# Fritzing sketch resistencia-para-un-led-1 (saved by Fritzing 1.0.0rc)
breadboards: 1

parts:
  R3 = Resistor [tolerance=±5% power=0.25W resistance=100 package=THT]
  LED1 = LED - 5mm [color="Red (633nm)" current=0.030A package="5 mm [THT]"]
  VCC1 = 4 x AAA Battery Mount

nets:
  N1: R3.Pin_0, LED1.anode
  N2: R3.Pin_1, VCC1.+
  GND: LED1.cathode, VCC1.-
