# Fritzing sketch resistencia-para-un-led-2 (saved by Fritzing 1.0.0rc)
breadboards: 1

parts:
  R3 = Resistor [tolerance=±5% power=0.25W resistance=100 package=THT]
  LED1 = LED - 5mm [color="Red (633nm)" current=0.030A package="5 mm [THT]"]
  VCC1 = 4 x AAA Battery Mount
  P1 = Multimeter straight red probe
  P2 = Multimeter straight black probe
  OM1 = Multimeter (DC Voltage)

nets (from the schematic view):
  N1: R3.Pin_0, LED1.anode
  N2: R3.Pin_1, VCC1.+
  GND: LED1.cathode, VCC1.-, OM1.COM_Probe
  N3: P1.Probe_tip, P1.Probe_meter_end, P1.Probe_tip_2, OM1.V_Probe
  N4: P2.Probe_tip, P2.Probe_meter_end, P2.Probe_tip_2
