# Fritzing sketch resistencia-para-un-led-con-amperimetro (saved by Fritzing 1.0.0rc)
breadboards: 1

parts:
  R1 = Resistor [tolerance=±5% power=0.25W resistance=150 package=THT]
  VM4 = Multimeter (DC Current)
  VCC1 = 4 x AAA Battery Mount
  LED1 = LED - 3mm [color="Red (633nm)" current=20mA package="3 mm [THT]"]

nets:
  N1: R1.Pin_0, LED1.anode
  N2: R1.Pin_1, VM4.COM_Probe
  N3: VM4.A_Probe, VCC1.+
  GND: VCC1.-, LED1.cathode
