# Fritzing sketch resistencia-para-un-led-con-voltimetros (saved by Fritzing 1.0.0rc)
breadboards: 1

parts:
  LED1 = LED - 3mm [color="Red (633nm)" current=20mA package="3 mm [THT]"]
  R1 = Resistor [tolerance=±5% power=0.25W resistance=150 package=THT]
  VM1 = Multimeter (DC Voltage)
  VM2 = Multimeter (DC Voltage)
  VM3 = Multimeter (DC Voltage)
  VCC1 = 4 x AAA Battery Mount

nets:
  GND: LED1.cathode, VM1.COM_Probe, VM2.COM_Probe, VM2.V_Probe, VM3.COM_Probe, VCC1.-
  N1: LED1.anode, R1.Pin_0, VM1.V_Probe
  N2: R1.Pin_1, VM3.V_Probe, VCC1.+
