# Fritzing sketch resistencias-en-serie-1 (saved by Fritzing 0.9.3b)
breadboards: 1

parts:
  R1 = Resistor [tolerance=±5% resistance=100 package=THT]
  R2 = Resistor [tolerance=±5% resistance=200 package=THT]
  R3 = Resistor [tolerance=±5% resistance=150 package=THT]
  VCC1 = Battery block 9V
  R4 = Resistor [tolerance=±5% resistance=50 package=THT]

nets (from the schematic view):
  N1: R1.Pin_0, VCC1.-, VCC1.+, R4.Pin_1
  N2: R1.Pin_1, R2.Pin_0
  N3: R2.Pin_1, R3.Pin_0
  N4: R3.Pin_1, R4.Pin_0
