# Fritzing sketch resistencias-en-serie-y-paralelo-1 (saved by Fritzing 1.0.0rc)
breadboards: 1

parts:
  R1 = Resistor [tolerance=±5% power=0.25W resistance=220 package=THT]
  R2 = Resistor [tolerance=±5% power=0.25W resistance=220 package=THT]
  VCC1 = Battery
  R3 = Resistor [tolerance=±5% power=0.25W resistance=220 package=THT]
  R4 = Resistor [tolerance=±5% power=0.25W resistance=220 package=THT]

nets:
  N1: R1.Pin_0, VCC1.+
  N2: R1.Pin_1, R2.Pin_0, R3.Pin_0
  N3: R2.Pin_1, R4.Pin_0
  GND: VCC1.-, R3.Pin_1, R4.Pin_1
