# Fritzing sketch voltimetro-1 (saved by Fritzing 1.0.0rc)
breadboards: 1

parts:
  VM1 = Multimeter (DC Voltage)
  VCC1 = Battery block 9V

nets:
  GND: VM1.COM_Probe, VCC1.-
  N1: VM1.V_Probe, VCC1.+
