# Fritzing sketch voltimetro-dos-resistencias-en-serie (saved by Fritzing 1.0.0rc)
breadboards: 1

parts:
  VM1 = Multimeter (DC Voltage)
  R1 = Resistor [tolerance=±5% power=0.25W resistance=220 package=THT]
  VCC1 = 4 x AAA Battery Mount
  R3 = Resistor [tolerance=±5% power=0.25W resistance=330 package=THT]
  VM2 = Multimeter (DC Voltage)
  P1 = Multimeter straight red probe
  P2 = Multimeter straight black probe
  P3 = Multimeter straight red probe
  P4 = Multimeter straight black probe

nets:
  N1: VM1.COM_Probe, R1.Pin_0, R3.Pin_1, VM2.V_Probe, P2.Probe_tip, P2.Probe_meter_end, P2.Probe_tip_2, P3.Probe_tip, P3.Probe_meter_end
  N2: VM1.V_Probe, R1.Pin_1, VCC1.+, P1.Probe_tip, P1.Probe_meter_end
  GND: VCC1.-, R3.Pin_0, VM2.COM_Probe, P4.Probe_tip, P4.Probe_meter_end
